// Logisim project Relógio.circ as structural Verilog
module Clock_inicial (
  input  reset,
  output A,
  output B,
  output C,
  output D,
  output vai_1
);

  wire and_1_out, clock_1_out, d_ff_1_q, d_ff_1_qn, d_ff_2_q, d_ff_2_qn, d_ff_3_q, d_ff_3_qn, d_ff_4_q;

  Clock clock_1 (.out(clock_1_out));
  and and_1 (and_1_out, ~A, B, ~C, D);  // AND_Gate
  D_Flip_Flop d_ff_1 (.clk(clock_1_out), .D(A), .Q(d_ff_1_q), .Qn(d_ff_1_qn), .preset(vai_1));  // open: en, reset
  D_Flip_Flop d_ff_2 (.clk(d_ff_1_qn), .D(B), .Q(d_ff_2_q), .Qn(d_ff_2_qn), .preset(vai_1));  // open: en, reset
  D_Flip_Flop d_ff_3 (.clk(d_ff_2_qn), .D(C), .Q(d_ff_3_q), .Qn(d_ff_3_qn), .preset(vai_1));  // open: en, reset
  D_Flip_Flop d_ff_4 (.clk(d_ff_3_qn), .D(D), .Q(d_ff_4_q), .preset(vai_1));  // open: Qn, en, reset
  Multiplexer multiplexer_1 (.in0(and_1_out), .in1(reset), .out(vai_1), .sel(reset));  // open: en
  not not_1 (A, d_ff_1_q);
  not not_2 (B, d_ff_2_q);
  not not_3 (C, d_ff_3_q);
  not not_4 (D, d_ff_4_q);
endmodule
